// Logisim project ALU.circ as structural Verilog: 15 circuits, main circuit main
module main (
  input  [7:0] in_1,
  input  [7:0] in_2,
  input  [3:0] in_3
);

  wire and_1_out, n4_bit_alu_1_lsb_2, n4_bit_alu_1_msb_2, n4_bit_alu_1_zero, n4_bit_alu_2_lsb_2,
       n4_bit_alu_2_msb_2, n4_bit_alu_2_zero;
  wire [7:0] n4_bit_alu_1_q0;

  _4_Bit_ALU u_4_bit_alu_1 (
    .A0(in_1[0]), .A1(in_1[1]), .A2(in_1[2]), .A3(in_1[3]), .B0(in_2[0]), .B1(in_2[1]), .B2(in_2[2]),
    .B3(in_2[3]), .OP0(in_3[0]), .OP1(in_3[1]), .OP2(in_3[2]), .OP3(in_3[3]), .Mode(1'b0),
    .Zero(n4_bit_alu_1_zero), .Q0(n4_bit_alu_1_q0[0]), .Q1(n4_bit_alu_1_q0[1]), .Q2(n4_bit_alu_1_q0[2]),
    .Q3(n4_bit_alu_1_q0[3]), .MSB_2(n4_bit_alu_1_msb_2), .LSB_2(n4_bit_alu_1_lsb_2),
    .LSB(n4_bit_alu_2_msb_2), .MSB(n4_bit_alu_2_lsb_2));
  _4_Bit_ALU u_4_bit_alu_2 (
    .A0(in_1[4]), .A1(in_1[5]), .A2(in_1[6]), .A3(in_1[7]), .B0(in_2[4]), .B1(in_2[5]), .B2(in_2[6]),
    .B3(in_2[7]), .OP0(in_3[0]), .OP1(in_3[1]), .OP2(in_3[2]), .OP3(in_3[3]), .Mode(1'b1),
    .Zero(n4_bit_alu_2_zero), .Q0(n4_bit_alu_1_q0[4]), .Q1(n4_bit_alu_1_q0[5]), .Q2(n4_bit_alu_1_q0[6]),
    .Q3(n4_bit_alu_1_q0[7]), .MSB_2(n4_bit_alu_2_msb_2), .LSB_2(n4_bit_alu_2_lsb_2),
    .LSB(n4_bit_alu_1_msb_2), .MSB(n4_bit_alu_1_lsb_2));
  and and_1 (and_1_out, n4_bit_alu_1_zero, n4_bit_alu_2_zero);
  // Probe on and_1_out
  // Probe on n4_bit_alu_2_msb_2
  // Probe on n4_bit_alu_1_q0
endmodule

module _4_Bit_ALU (
  input  LSB,
  input  A0,
  input  A1,
  input  A2,
  input  A3,
  input  B0,
  input  B1,
  input  B2,
  input  B3,
  input  MSB,
  input  OP0,
  input  OP1,
  input  OP2,
  input  OP3,
  input  Mode,
  output Zero,
  output LSB_2,
  output Q0,
  output Q1,
  output Q2,
  output Q3,
  output MSB_2
);

  wire [3:0] add_op_1_q, and_op_1_q, b2a_op_1_q, dec_op_1_q, inc_op_1_q, neg_op_1_q, not_or_1_q, or_op_1_q,
       rth_op_1_q, rtl_op_1_q, sub_op_1_q, xor_op_1_q;
  wire [5:0] add_op_1_lsb_2, and_op_1_lsb_2, b2a_op_1_lsb_2, dec_op_1_lsb_2, inc_op_1_lsb_2, neg_op_1_lsb_2,
       not_or_1_lsb_2, or_op_1_lsb_2, rth_op_1_lsb_2, rtl_op_1_lsb_2, sub_op_1_lsb_2, xor_op_1_lsb_2;

  ADD_OP add_op_1 (
    .A({A3, A2, A1, A0}), .B({B3, B2, B1, B0}), .LSB(LSB), .Mode(Mode), .LSB_2(add_op_1_lsb_2[0]),
    .Q(add_op_1_q), .MSB_2(add_op_1_lsb_2[5]), .MSB(MSB));
  SUB_OP sub_op_1 (
    .A({A3, A2, A1, A0}), .B({B3, B2, B1, B0}), .LSB(LSB), .Mode(Mode), .LSB_2(sub_op_1_lsb_2[0]),
    .Q(sub_op_1_q), .MSB_2(sub_op_1_lsb_2[5]), .MSB(MSB));
  INC_OP inc_op_1 (
    .LSB(LSB), .A({A3, A2, A1, A0}), .B({B3, B2, B1, B0}), .MSB(MSB), .Mode(Mode), .LSB_2(inc_op_1_lsb_2[0]),
    .Q(inc_op_1_q), .MSB_2(inc_op_1_lsb_2[5]));
  DEC_OP dec_op_1 (
    .LSB(LSB), .A({A3, A2, A1, A0}), .B({B3, B2, B1, B0}), .MSB(MSB), .Mode(Mode), .LSB_2(dec_op_1_lsb_2[0]),
    .Q(dec_op_1_q), .MSB_2(dec_op_1_lsb_2[5]));
  RTL_OP rtl_op_1 (
    .LSB(LSB), .A({A3, A2, A1, A0}), .B({B3, B2, B1, B0}), .MSB(MSB), .Mode(Mode), .LSB_2(rtl_op_1_lsb_2[0]),
    .Q(rtl_op_1_q), .MSB_2(rtl_op_1_lsb_2[5]));
  RTH_OP rth_op_1 (
    .LSB(LSB), .A({A3, A2, A1, A0}), .B({B3, B2, B1, B0}), .MSB(MSB), .Mode(Mode), .LSB_2(rth_op_1_lsb_2[0]),
    .Q(rth_op_1_q), .MSB_2(rth_op_1_lsb_2[5]));
  B2A_OP b2a_op_1 (
    .LSB(LSB), .A({A3, A2, A1, A0}), .B({B3, B2, B1, B0}), .MSB(MSB), .Mode(Mode), .LSB_2(b2a_op_1_lsb_2[0]),
    .Q(b2a_op_1_q), .MSB_2(b2a_op_1_lsb_2[5]));
  NEG_OP neg_op_1 (
    .LSB(LSB), .A({A3, A2, A1, A0}), .B({B3, B2, B1, B0}), .MSB(MSB), .Mode(Mode), .LSB_2(neg_op_1_lsb_2[0]),
    .Q(neg_op_1_q), .MSB_2(neg_op_1_lsb_2[5]));
  AND_OP and_op_1 (
    .LSB(LSB), .A({A3, A2, A1, A0}), .B({B3, B2, B1, B0}), .MSB(MSB), .Mode(Mode), .LSB_2(and_op_1_lsb_2[0]),
    .Q(and_op_1_q), .MSB_2(and_op_1_lsb_2[5]));
  OR_OP or_op_1 (
    .LSB(LSB), .A({A3, A2, A1, A0}), .B({B3, B2, B1, B0}), .MSB(MSB), .Mode(Mode), .LSB_2(or_op_1_lsb_2[0]),
    .Q(or_op_1_q), .MSB_2(or_op_1_lsb_2[5]));
  XOR_OP xor_op_1 (
    .LSB(LSB), .A({A3, A2, A1, A0}), .B({B3, B2, B1, B0}), .MSB(MSB), .Mode(Mode), .LSB_2(xor_op_1_lsb_2[0]),
    .Q(xor_op_1_q), .MSB_2(xor_op_1_lsb_2[5]));
  NOT_OR not_or_1 (
    .LSB(LSB), .A({A3, A2, A1, A0}), .B({B3, B2, B1, B0}), .MSB(MSB), .Mode(Mode), .LSB_2(not_or_1_lsb_2[0]),
    .Q(not_or_1_q), .MSB_2(not_or_1_lsb_2[5]));
  Multiplexer #(.select(4), .width(6)) multiplexer_1 (
    .in0({add_op_1_lsb_2[5], add_op_1_q, add_op_1_lsb_2[0]}),
    .in1({sub_op_1_lsb_2[5], sub_op_1_q, sub_op_1_lsb_2[0]}),
    .in2({inc_op_1_lsb_2[5], inc_op_1_q, inc_op_1_lsb_2[0]}),
    .in3({dec_op_1_lsb_2[5], dec_op_1_q, dec_op_1_lsb_2[0]}),
    .in4({rtl_op_1_lsb_2[5], rtl_op_1_q, rtl_op_1_lsb_2[0]}),
    .in5({rth_op_1_lsb_2[5], rth_op_1_q, rth_op_1_lsb_2[0]}),
    .in6({b2a_op_1_lsb_2[5], b2a_op_1_q, b2a_op_1_lsb_2[0]}),
    .in7({neg_op_1_lsb_2[5], neg_op_1_q, neg_op_1_lsb_2[0]}),
    .in8({and_op_1_lsb_2[5], and_op_1_q, and_op_1_lsb_2[0]}),
    .in9({or_op_1_lsb_2[5], or_op_1_q, or_op_1_lsb_2[0]}),
    .in10({xor_op_1_lsb_2[5], xor_op_1_q, xor_op_1_lsb_2[0]}),
    .in11({not_or_1_lsb_2[5], not_or_1_q, not_or_1_lsb_2[0]}), .in12({6{1'b0}}), .in13({6{1'b0}}),
    .in14({6{1'b0}}), .in15({6{1'b0}}), .out({MSB_2, Q3, Q2, Q1, Q0, LSB_2}), .sel({OP3, OP2, OP1, OP0}));  // open: en
  nor nor_1 (Zero, Q0, Q1, Q2, Q3);
endmodule

module ADD_OP (
  input  LSB,
  input  [3:0] A,
  input  [3:0] B,
  input  MSB,
  input  Mode,
  output LSB_2,
  output [3:0] Q,
  output MSB_2
);

  wire and_1_out;

  and and_1 (and_1_out, LSB, Mode);
  Adder #(.width(4)) adder_1 (.a(A), .b(B), .out(Q), .cin(and_1_out), .cout(MSB_2));

  assign LSB_2 = 1'b0;
endmodule

module SUB_OP (
  input  LSB,
  input  [3:0] A,
  input  [3:0] B,
  input  MSB,
  input  Mode,
  output LSB_2,
  output [3:0] Q,
  output MSB_2
);

  wire and_1_out;

  and and_1 (and_1_out, LSB, Mode);
  Subtractor #(.width(4)) subtractor_1 (.a(A), .b(B), .out(Q), .bin(and_1_out), .bout(MSB_2));

  assign LSB_2 = 1'b0;
endmodule

module INC_OP (
  input  LSB,
  input  [3:0] A,
  input  [3:0] B,
  input  MSB,
  input  Mode,
  output LSB_2,
  output [3:0] Q,
  output MSB_2
);

  wire and_1_out;
  wire [3:0] multiplexer_1_out;

  and and_1 (and_1_out, LSB, Mode);
  Multiplexer #(.width(4)) multiplexer_1 (
    .in0(4'b0001), .in1(4'b0000), .out(multiplexer_1_out), .sel(Mode));  // open: en
  Adder #(.width(4)) adder_1 (.a(A), .b(multiplexer_1_out), .out(Q), .cin(and_1_out), .cout(MSB_2));

  assign LSB_2 = 1'b0;
endmodule

module DEC_OP (
  input  LSB,
  input  [3:0] A,
  input  [3:0] B,
  input  MSB,
  input  Mode,
  output LSB_2,
  output [3:0] Q,
  output MSB_2
);

  wire and_1_out;
  wire [3:0] multiplexer_1_out;

  and and_1 (and_1_out, LSB, Mode);
  Multiplexer #(.width(4)) multiplexer_1 (
    .in0(4'b0001), .in1(4'b0000), .out(multiplexer_1_out), .sel(Mode));  // open: en
  Subtractor #(.width(4)) subtractor_1 (.a(A), .b(multiplexer_1_out), .out(Q), .bin(and_1_out), .bout(MSB_2));

  assign LSB_2 = 1'b0;
endmodule

module RTL_OP (
  input  LSB,
  input  [3:0] A,
  input  [3:0] B,
  input  MSB,
  input  Mode,
  output LSB_2,
  output [3:0] Q,
  output MSB_2
);


  assign LSB_2 = A[0];
  assign MSB_2 = 1'b0;
  assign Q = {MSB, A[3:1]};
endmodule

module RTH_OP (
  input  LSB,
  input  [3:0] A,
  input  [3:0] B,
  input  MSB,
  input  Mode,
  output LSB_2,
  output [3:0] Q,
  output MSB_2
);


  assign LSB_2 = 1'b0;
  assign MSB_2 = A[3];
  assign Q = {A[2:0], LSB};
endmodule

module B2A_OP (
  input  LSB,
  input  [3:0] A,
  input  [3:0] B,
  input  MSB,
  input  Mode,
  output LSB_2,
  output [3:0] Q,
  output MSB_2
);


  assign LSB_2 = 1'b0;
  assign MSB_2 = 1'b0;
  assign Q = B;
endmodule

module NEG_OP (
  input  LSB,
  input  [3:0] A,
  input  [3:0] B,
  input  MSB,
  input  Mode,
  output LSB_2,
  output [3:0] Q,
  output MSB_2
);

  wire and_1_out;
  wire [3:0] multiplexer_1_out, not_1_out;

  and and_1 (and_1_out, LSB, Mode);
  assign not_1_out = ~A;  // NOT_Gate not_1, 4 bits wide
  Multiplexer #(.width(4)) multiplexer_1 (
    .in0(4'b0001), .in1(4'b0000), .out(multiplexer_1_out), .sel(Mode));  // open: en
  Adder #(.width(4)) adder_1 (.a(not_1_out), .b(multiplexer_1_out), .out(Q), .cin(and_1_out), .cout(MSB_2));

  assign LSB_2 = 1'b0;
endmodule

module AND_OP (
  input  LSB,
  input  [3:0] A,
  input  [3:0] B,
  input  MSB,
  input  Mode,
  output LSB_2,
  output [3:0] Q,
  output MSB_2
);

  assign Q = A & B;  // AND_Gate and_1, 4 bits wide

  assign LSB_2 = 1'b0;
  assign MSB_2 = 1'b0;
endmodule

module OR_OP (
  input  LSB,
  input  [3:0] A,
  input  [3:0] B,
  input  MSB,
  input  Mode,
  output LSB_2,
  output [3:0] Q,
  output MSB_2
);

  assign Q = A | B;  // OR_Gate or_1, 4 bits wide

  assign LSB_2 = 1'b0;
  assign MSB_2 = 1'b0;
endmodule

module XOR_OP (
  input  LSB,
  input  [3:0] A,
  input  [3:0] B,
  input  MSB,
  input  Mode,
  output LSB_2,
  output [3:0] Q,
  output MSB_2
);

  assign Q = A ^ B;  // XOR_Gate xor_1, 4 bits wide

  assign LSB_2 = 1'b0;
  assign MSB_2 = 1'b0;
endmodule

module NOT_OR (
  input  LSB,
  input  [3:0] A,
  input  [3:0] B,
  input  MSB,
  input  Mode,
  output LSB_2,
  output [3:0] Q,
  output MSB_2
);

  assign Q = ~A;  // NOT_Gate not_1, 4 bits wide

  assign LSB_2 = 1'b0;
  assign MSB_2 = 1'b0;
endmodule

module Truth_Table_Extraction_Circuit (
);

  wire button_1_out, CLK, clock_1_out, counter_1_carry, j_k_ff_1_q;
  wire [7:0] ram_1_data;
  wire [14:0] counter_1_q;

  Clock clock_1 (.out(clock_1_out));
  Button button_1 (.out(button_1_out));
  and and_1 (CLK, clock_1_out, j_k_ff_1_q);
  J_K_Flip_Flop j_k_ff_1 (
    .J(button_1_out), .clk(clock_1_out), .K(counter_1_carry), .Q(j_k_ff_1_q));  // open: Qn, preset, en, reset
  Counter #(.width(15), .max('h7fff), .trigger("falling")) counter_1 (
    .Q(counter_1_q), .carry(counter_1_carry), .clk(CLK));  // open: load, D, count, clr
  RAM #(.addrWidth(15)) ram_1 (.addr(counter_1_q), .data(ram_1_data), .clk(CLK), .ld(1'b0));  // open: sel, clr
  _4_Bit_ALU u_4_bit_alu_1 (
    .A0(counter_1_q[0]), .A1(counter_1_q[1]), .A2(counter_1_q[2]), .A3(counter_1_q[3]), .B0(counter_1_q[4]),
    .B1(counter_1_q[5]), .B2(counter_1_q[6]), .B3(counter_1_q[7]), .OP0(counter_1_q[11]),
    .OP1(counter_1_q[9]), .OP2(counter_1_q[8]), .OP3(counter_1_q[13]), .Mode(counter_1_q[10]),
    .Zero(ram_1_data[3]), .Q0(ram_1_data[4]), .Q1(ram_1_data[5]), .Q2(ram_1_data[6]), .Q3(ram_1_data[7]),
    .MSB_2(ram_1_data[2]), .LSB_2(ram_1_data[1]), .LSB(counter_1_q[14]), .MSB(counter_1_q[12]));
  // also tied to GND on the sheet: ram_1_data[0]
endmodule
