// Logisim project EEPROM Write Enable Clock.circ as structural Verilog: 1 circuit, main circuit main
module main (
  input  MWE,
  input  RST,
  input  MWE_2,
  input  RST_2
);

  wire CLK_out, dip_7400_1_p2, dip_7400_1_p3, dip_7400_1_p4, dip_7400_1_p5, dip_7402_1_p2, dip_7402_1_p4,
       dip_7402_1_p5, dip_7402_1_p10, dip_7402_1_p11, dip_7402_1_p16, nand_1_out, nand_2_out, nand_3_out,
       nand_4_out, nor_1_out, nor_2_out, nor_4_out;

  Clock CLK (.out(CLK_out));
  nor nor_1 (nor_1_out, MWE, MWE);
  // DIP_7400 dip_7400_1: pin names not known; wires that end beside it: MWE_2, dip_7400_1_p2, dip_7400_1_p3, dip_7400_1_p4, dip_7400_1_p5, dip_7400_1_p4
  Clock CLK_2 (.out(dip_7400_1_p2));
  nand nand_1 (nand_1_out, nor_1_out, CLK_out);
  nand nand_2 (nand_2_out, CLK_out, MWE);
  // DIP_7402 dip_7402_1: pin names not known; wires that end beside it: dip_7400_1_p5, dip_7402_1_p2, 1'b1, dip_7402_1_p4, dip_7402_1_p5, dip_7402_1_p2, dip_7400_1_p3, RST_2, MWE_2, dip_7402_1_p10, dip_7402_1_p11, dip_7402_1_p5, dip_7402_1_p4, dip_7402_1_p10, dip_7402_1_p11, dip_7402_1_p16
  nor nor_2 (nor_2_out, MWE, RST);
  nand nand_3 (nand_3_out, 1'b1, nand_1_out);
  nor nor_3 (dip_7402_1_p16, nand_3_out, nor_4_out);
  nor nor_4 (nor_4_out, dip_7402_1_p16, nand_4_out);
  nand nand_4 (nand_4_out, nand_2_out, nor_2_out);
endmodule
