// Logisim project LOTP_8-Bit-CPU-V4.circ as structural Verilog: 3 circuits, main circuit Main
module Main (
  input  in_1,
  output out_2
);

  wire button_1_out, clock_1_out;
  wire [7:0] controlled_buffer_1_out, cpu_1_out_5, rom_1_data;

  // Probe on cpu_1_out_5
  ROM rom_1 (.addr(cpu_1_out_5), .data(rom_1_data));  // open: sel
  assign controlled_buffer_1_out = in_1 ? rom_1_data : 8'bz;  // Controlled_Buffer controlled_buffer_1
  CPU cpu_1 (
    .in_1(controlled_buffer_1_out), .out_5(cpu_1_out_5), .OUTRDY(out_2), .CLK(clock_1_out),
    .BOOTLOADER(in_1), .RST(button_1_out));
  Button button_1 (.out(button_1_out));
  Clock clock_1 (.out(clock_1_out));

  // Notes on the sheet:
  //   contents of rom_1 (hex, n*v repeats v):
  //   1 1 4 1 5 6 8 a 7 5 7 a
endmodule

module CPU (
  input  [7:0] in_1,
  input  RST,
  input  BOOTLOADER,
  input  CLK,
  output [7:0] out_5,
  output OUTRDY
);

  wire CLK_t, Counter_Up, d_ff_1_qn, EOP, HALT, Halt_t, nor_1_out, not_1_out, not_2_out, not_3_out,
       not_4_out, Overflow, R_ALU, R_AREG, R_Counter, R_INPUT, R_IREG, R_PrgEEPROM, R_STKMEM,
       Reset_Microcode, StackDown, StackUp, W_ADR_REG, W_AREG, W_BREG, W_CALREG, W_Counter, W_IREG,
       W_PrgEEPROM, W_STKMEM, Zero;
  wire [3:0] counter_1_q, register_3_q;
  wire [7:0] alu_1_c, BUS, controlled_buffer_3_out, controlled_buffer_8_out, counter_2_q, counter_3_q,
       register_1_q, register_2_q, register_5_q, register_6_q, rom_1_data;
  wire [7:5] rom_2_data;

  assign BUS = R_IREG ? register_1_q : 8'bz;  // Controlled_Buffer controlled_buffer_1
  Counter #(.width(4), .max('hf)) counter_1 (
    .load(Reset_Microcode), .D(4'b0000), .count(not_1_out), .Q(counter_1_q), .clk(not_2_out), .clr(RST));  // open: carry
  not not_1 (not_1_out, Reset_Microcode);
  not not_2 (not_2_out, CLK_t);
  Register register_1 (.D(BUS), .en(W_IREG), .Q(register_1_q), .clk(CLK_t), .clr(RST));
  Decoder #(.select(4), .disabled(0), .enable("false")) decoder_1 (
    .out1(R_Counter), .out2(R_PrgEEPROM), .out3(R_IREG), .out4(R_AREG), .out5(R_INPUT), .out6(R_STKMEM),
    .out7(R_ALU), .sel(rom_1_data[3:0]));  // open: out0, out8, out9, out10, out11, out12, out13, out14, out15
  ROM #(.addrWidth(11)) rom_1 (
    .addr({BOOTLOADER, Overflow, Zero, register_1_q[3:0], counter_1_q}), .data(rom_1_data));  // open: sel
  ROM #(.addrWidth(11)) rom_2 (
    .addr({BOOTLOADER, Overflow, Zero, register_1_q[3:0], counter_1_q}),
    .data({rom_2_data, Reset_Microcode, StackDown, StackUp, Counter_Up, Halt_t}));  // open: sel
  Register register_2 (.D(BUS), .en(W_ADR_REG), .Q(register_2_q), .clk(CLK_t), .clr(RST));
  Decoder #(.select(4), .disabled(0), .enable("false")) decoder_2 (
    .out1(W_Counter), .out2(W_ADR_REG), .out3(W_PrgEEPROM), .out4(W_IREG), .out5(W_AREG), .out6(W_BREG),
    .out7(W_CALREG), .out8(OUTRDY), .out9(W_STKMEM), .sel(rom_1_data[7:4]));  // open: out0, out10, out11, out12, out13, out14, out15
  Counter counter_2 (
    .load(W_Counter), .D(BUS), .count(Counter_Up), .Q(counter_2_q), .carry(EOP), .clk(CLK_t), .clr(RST));
  assign BUS = R_Counter ? counter_2_q : 8'bz;  // Controlled_Buffer controlled_buffer_2
  assign controlled_buffer_3_out = W_PrgEEPROM ? BUS : 8'bz;  // Controlled_Buffer controlled_buffer_3
  RAM ram_1 (.addr(register_2_q), .data(controlled_buffer_3_out), .clk(CLK_t), .ld(not_3_out));  // open: sel, clr
  not not_3 (not_3_out, W_PrgEEPROM);
  assign BUS = R_PrgEEPROM ? controlled_buffer_3_out : 8'bz;  // Controlled_Buffer controlled_buffer_4
  assign BUS = R_INPUT ? in_1 : 8'bz;  // Controlled_Buffer controlled_buffer_5
  assign BUS = R_AREG ? register_5_q : 8'bz;  // Controlled_Buffer controlled_buffer_6
  Register #(.width(4)) register_3 (.D(BUS[7:4]), .en(W_CALREG), .Q(register_3_q), .clk(CLK_t), .clr(RST));
  assign BUS = R_ALU ? alu_1_c : 8'bz;  // Controlled_Buffer controlled_buffer_7
  nor nor_1 (nor_1_out, StackUp, StackDown);
  Counter counter_3 (.load(nor_1_out), .count(StackUp), .Q(counter_3_q), .clk(CLK_t), .clr(RST));  // open: D, carry
  Register register_4 (.D(BUS), .en(OUTRDY), .Q(out_5), .clk(CLK_t), .clr(RST));
  Register register_5 (.D(BUS), .en(W_AREG), .Q(register_5_q), .clk(CLK_t), .clr(RST));
  ALU alu_1 (.CAL(register_3_q), .A(register_5_q), .C(alu_1_c), .Zero(Zero), .Overflow(Overflow), .B(register_6_q));
  Register register_6 (.D(BUS), .en(W_BREG), .Q(register_6_q), .clk(CLK_t), .clr(RST));
  D_Flip_Flop d_ff_1 (.clk(CLK_t), .D(Halt_t), .Qn(d_ff_1_qn), .reset(RST));  // open: Q, preset, en
  not not_4 (not_4_out, W_STKMEM);
  and and_1 (CLK_t, d_ff_1_qn, CLK);
  assign controlled_buffer_8_out = W_STKMEM ? BUS : 8'bz;  // Controlled_Buffer controlled_buffer_8
  RAM ram_2 (.addr(counter_3_q), .data(controlled_buffer_8_out), .clk(CLK_t), .ld(not_4_out), .clr(RST));  // open: sel
  assign BUS = R_STKMEM ? controlled_buffer_8_out : 8'bz;  // Controlled_Buffer controlled_buffer_9
  LED led_1 (.in(R_Counter));
  LED led_2 (.in(R_PrgEEPROM));
  LED led_3 (.in(R_IREG));
  LED led_4 (.in(R_AREG));
  LED led_5 (.in(R_INPUT));
  LED led_6 (.in(R_STKMEM));
  LED led_7 (.in(R_ALU));
  LED led_8 (.in(W_Counter));
  LED led_9 (.in(W_ADR_REG));
  LED led_10 (.in(W_PrgEEPROM));
  LED led_11 (.in(W_IREG));
  LED led_12 (.in(W_AREG));
  LED led_13 (.in(W_BREG));
  LED led_14 (.in(W_CALREG));
  LED led_15 (.in(OUTRDY));
  LED led_16 (.in(W_STKMEM));
  LED led_17 (.in(HALT));
  LED led_18 (.in(Counter_Up));
  LED led_19 (.in(StackUp));
  LED led_20 (.in(StackDown));
  LED led_21 (.in(Reset_Microcode));
  LED led_22 (.in(CLK_t));
  // Probe on BUS
  // Probe on BUS
  // Probe on BUS
  // Probe on out_5
  // Probe on out_5

  // Other names for the same wires on the sheet: INPUT[7:0] = in_1; OUTPUT[7:0] = out_5; OUTPUT_READY = OUTRDY;
  //   W_OUT = OUTRDY

  // Notes on the sheet:
  //   Instruction
  //   Register
  //   Microcode EEPROM A
  //   Microcode EEPROM B
  //   Read 
  //   contents of rom_1 (hex, n*v repeats v):
  //   21 42 14*0 21 42 21 52 12*0 21 42 21 22 52 11*0 21 42 21 22 34 11*0 21 42 21 62 12*0 21 42 73 13*0
  //   21 42 57 13*0 21 42 21 12 12*0 21 42 14*0 21 42 14*0 21 42 94 13*0 21 42 0 56 12*0 21 42 55 13*0 21
  //   42 84 13*0 21 42 14*0 21 42 14*0 21 42 14*0 21 42 21 52 12*0 21 42 21 22 52 11*0 21 42 21 22 34 11*0
  //   21 42 21 62 12*0 21 42 73 13*0 21 42 57 13*0 21 42 21 12 12*0 21 42 21 12 12*0 21 42 14*0 21 42 94
  //   13*0 21 42 0 56 12*0 21 42 55 13*0 21 42 84 13*0 21 42 14*0 21 42 14*0 21 42 14*0 21 42 21 52 12*0
  //   21 42 21 22 52 11*0 21 42 21 22 34 11*0 21 42 21 62 12*0 21 42 73 13*0 21 42 57 13*0 21 42 21 12
  //   12*0 21 42 14*0 21 42 21 12 12*0 21 42 94 13*0 21 42 0 56 12*0 21 42 55 13*0 21 42 84 13*0 21 42
  //   14*0 21 42 14*0 21 42 14*0 21 42 21 52 12*0 21 42 21 22 52 11*0 21 42 21 22 34 11*0 21 42 21 62 12*0
  //   21 42 73 13*0 21 42 57 13*0 21 42 21 12 12*0 21 42 21 12 12*0 21 42 21 12 12*0 21 42 94 13*0 21 42 0
  //   56 12*0 21 42 55 13*0 21 42 84 13*0 21 42 14*0 21 42 14*0 21 0 0 84 35 51 5*0 61 4*0 21 0 0 84 35 51
  //   5*0 61 4*0 21 0 0 84 35 51 5*0 61 4*0 21 0 0 84 35 51 5*0 61 4*0 21 0 0 84 35 51 5*0 61 4*0 21 0 0
  //   84 35 51 5*0 61 4*0 21 0 0 84 35 51 5*0 61 4*0 21 0 0 84 35 51 5*0 61 4*0 21 0 0 84 35 51 5*0 61 4*0
  //   21 0 0 84 35 51 5*0 61 4*0 21 0 0 84 35 51 5*0 61 4*0 21 0 0 84 35 51 5*0 61 4*0 21 0 0 84 35 51 5*0
  //   61 4*0 21 0 0 84 35 51 5*0 61 4*0 21 0 0 84 35 51 5*0 61 4*0 21 0 0 84 35 51 5*0 61 4*0 21 0 61 8*0
  //   61 81 21 0 0 21 0 61 8*0 61 81 21 0 0 21 0 61 8*0 61 81 21 0 0 21 0 61 8*0 61 81 21 0 0 21 0 61 8*0
  //   61 81 21 0 0 21 0 61 8*0 61 81 21 0 0 21 0 61 8*0 61 81 21 0 0 21 0 61 8*0 61 81 21 0 0 21 0 61 8*0
  //   61 81 21 0 0 21 0 61 8*0 61 81 21 0 0 21 0 61 8*0 61 81 21 0 0 21 0 61 8*0 61 81 21 0 0 21 0 61 8*0
  //   61 81 21 0 0 21 0 61 8*0 61 81 21 0 0 21 0 61 8*0 61 81 21 0 0 21 0 61 8*0 61 81 21 258*0 21 5*0 21
  //   0 84 35 51 5*0 21 5*0 21 0 84 35 51 5*0 21 5*0 21 0 84 35 51 5*0 21 5*0 21 0 84 35 51 5*0 21 5*0 21
  //   0 84 35 51 5*0 21 5*0 21 0 84 35 51 5*0 21 5*0 21 0 84 35 51 5*0 21 5*0 21 0 84 35 51 5*0 21 5*0 21
  //   0 84 35 51 5*0 21 5*0 21 0 84 35 51 5*0 21 5*0 21 0 84 35 51 5*0 21 5*0 21 0 84 35 51 5*0 21 5*0 21
  //   0 84 35 51 5*0 21 5*0 21 0 84 35 51 5*0 21 5*0 21 0 84 35 51 5*0 21 5*0 21 0 84 35 51
  //   contents of rom_2 (hex, n*v repeats v):
  //   0 2 10 14*0 2 0 2 10 12*0 2 0 2 0 10 11*0 2 0 2 0 10 11*0 2 0 2 10 12*0 2 0 10 13*0 2 0 10 13*0 2 0
  //   0 10 12*0 2 12 14*0 2 12 14*0 2 0 4 10 12*0 2 8 0 10 12*0 2 0 10 13*0 2 0 10 13*0 2 10 14*0 2 11
  //   14*0 2 10 14*0 2 0 2 10 12*0 2 0 2 0 10 11*0 2 0 2 0 10 11*0 2 0 2 10 12*0 2 0 10 13*0 2 0 10 13*0 2
  //   0 0 10 12*0 2 0 0 10 12*0 2 12 14*0 2 0 4 10 12*0 2 8 0 10 12*0 2 0 10 13*0 2 0 10 13*0 2 10 14*0 2
  //   11 14*0 2 10 14*0 2 0 2 10 12*0 2 0 2 0 10 11*0 2 0 2 0 10 11*0 2 0 2 10 12*0 2 0 10 13*0 2 0 10
  //   13*0 2 0 0 10 12*0 2 12 14*0 2 0 0 10 12*0 2 0 4 10 12*0 2 8 0 10 12*0 2 0 10 13*0 2 0 10 13*0 2 10
  //   14*0 2 11 14*0 2 10 14*0 2 0 2 10 12*0 2 0 2 0 10 11*0 2 0 2 0 10 11*0 2 0 2 10 12*0 2 0 10 13*0 2 0
  //   10 13*0 2 0 0 10 12*0 2 0 0 10 12*0 2 0 0 10 12*0 2 0 4 10 12*0 2 8 0 10 12*0 2 0 10 13*0 2 0 10
  //   13*0 2 10 14*0 2 11 14*0 2 4*0 10 10*0 2 4*0 10 10*0 2 4*0 10 10*0 2 4*0 10 10*0 2 4*0 10 10*0 2 4*0
  //   10 10*0 2 4*0 10 10*0 2 4*0 10 10*0 2 4*0 10 10*0 2 4*0 10 10*0 2 4*0 10 10*0 2 4*0 10 10*0 2 4*0 10
  //   10*0 2 4*0 10 10*0 2 4*0 10 10*0 2 4*0 10 10*0 2 12*0 11 0 0 2 12*0 11 0 0 2 12*0 11 0 0 2 12*0 11 0
  //   0 2 12*0 11 0 0 2 12*0 11 0 0 2 12*0 11 0 0 2 12*0 11 0 0 2 12*0 11 0 0 2 12*0 11 0 0 2 12*0 11 0 0
  //   2 12*0 11 0 0 2 12*0 11 0 0 2 12*0 11 0 0 2 12*0 11 0 0 2 12*0 11 258*0 2 5*0 2 0 0 0 11 5*0 2 5*0 2
  //   0 0 0 11 5*0 2 5*0 2 0 0 0 11 5*0 2 5*0 2 0 0 0 11 5*0 2 5*0 2 0 0 0 11 5*0 2 5*0 2 0 0 0 11 5*0 2
  //   5*0 2 0 0 0 11 5*0 2 5*0 2 0 0 0 11 5*0 2 5*0 2 0 0 0 11 5*0 2 5*0 2 0 0 0 11 5*0 2 5*0 2 0 0 0 11
  //   5*0 2 5*0 2 0 0 0 11 5*0 2 5*0 2 0 0 0 11 5*0 2 5*0 2 0 0 0 11 5*0 2 5*0 2 0 0 0 11 5*0 2 5*0 2 0 0
  //   0 11
  //   Write
  //   Calculation Register
  //   A Register
  //   B Register
  //   OUTPUT
  //   INPUT
endmodule

module ALU (
  input  [7:0] A,
  input  [7:0] B,
  input  [3:0] CAL,
  output Zero,
  output [7:0] C,
  output Overflow
);

  wire n4_bit_alu_1_lsb_2, n4_bit_alu_1_msb_2, n4_bit_alu_1_zero, n4_bit_alu_2_lsb_2, n4_bit_alu_2_zero;

  _4_Bit_ALU u_4_bit_alu_1 (
    .A0(A[0]), .A1(A[1]), .A2(A[2]), .A3(A[3]), .B0(B[0]), .B1(B[1]), .B2(B[2]), .B3(B[3]), .OP0(CAL[0]),
    .OP1(CAL[1]), .OP2(CAL[2]), .OP3(CAL[3]), .Mode(1'b0), .Zero(n4_bit_alu_1_zero), .Q0(C[0]), .Q1(C[1]),
    .Q2(C[2]), .Q3(C[3]), .MSB_2(n4_bit_alu_1_msb_2), .LSB_2(n4_bit_alu_1_lsb_2), .LSB(Overflow),
    .MSB(n4_bit_alu_2_lsb_2));
  _4_Bit_ALU u_4_bit_alu_2 (
    .A0(A[4]), .A1(A[5]), .A2(A[6]), .A3(A[7]), .B0(B[4]), .B1(B[5]), .B2(B[6]), .B3(B[7]), .OP0(CAL[0]),
    .OP1(CAL[1]), .OP2(CAL[2]), .OP3(CAL[3]), .Mode(1'b1), .Zero(n4_bit_alu_2_zero), .Q0(C[4]), .Q1(C[5]),
    .Q2(C[6]), .Q3(C[7]), .MSB_2(Overflow), .LSB_2(n4_bit_alu_2_lsb_2), .LSB(n4_bit_alu_1_msb_2),
    .MSB(n4_bit_alu_1_lsb_2));
  and and_1 (Zero, n4_bit_alu_1_zero, n4_bit_alu_2_zero);
endmodule
